# Fritzing sketch V2.4 (saved by Fritzing 0.9.4)
circuit board: 5cm x 7cm
breadboards: 1

parts:
  JP1 = FTDI_BASIC [package=ftdi_basic]
  JP3 = FTDI_BASIC [package=ftdi_basic]
  JP4 = FTDI_BASIC [package=ftdi_basic]
  NANO = Arduino Nano (Rev3.0)
  IC = UAA2022
  U1 = Voltage Regulator - 5V [package="TO220 [THT]"]
  Q1 = PNP-Transistor [package="TO92 [THT]"]
  J1 = female pin header, 2 pins [form="♀ (female)"]
  J2 = female pin header, 2 pins [form="♀ (female)"]
  47kΩ = Resistor [tolerance=±0.1% resistance=47k package=THT]
  100µF = Electrolytic Capacitor [capacitance=100µF voltage=16V package="100 mil [THT, electrolytic]"]
  J4 = female pin header, 2 pins [form="♀ (female)"]
  J5 = female pin header, 2 pins [form="♀ (female)"]
  J6 = female pin header, 2 pins [form="♀ (female)"]
  J7 = female pin header, 2 pins [form="♀ (female)"]
  PHOTO = Photocell (LDR) [package=THT]
  JP2 = FTDI_BASIC [package=ftdi_basic]
  6_8kΩ = Resistor [tolerance=±5% resistance=6.8k package=THT]
  100kΩ = Resistor [tolerance=±5% resistance=100k package=THT]
  330Ω = Resistor [tolerance=±5% resistance=330 package=THT]
  10kΩ = Resistor [tolerance=±5% resistance=10k package=THT]

nets:
  N1: JP1.5, IC.Out_7
  N2: JP1.3, IC.Out_9
  N3: JP1.4, IC.Out_8
  5V: JP3.1, NANO.5V, IC.VCC, IC.LED_TEST, U1.output_voltage, 100µF.+, J4.pin2, J5.pin1, PHOTO.pin_1, JP2.1
  N4: JP3.2, IC.OUT_15
  N5: JP3.3, IC.OUT_16
  N6: JP3.4, IC.Out_1
  N7: JP4.5, IC.Out_6
  N8: JP4.1, IC.Out_2
  N9: JP4.2, IC.Out_3
  N10: JP4.3, IC.Out_4
  N11: JP4.4, IC.Out_5
  GND: NANO.GND, IC.GND, U1.GND, Q1.E, J2.pin2, 100µF.-, J4.pin1, J5.pin2, 100kΩ.Pin_1
  N12: NANO.D2, 10kΩ.Pin_1
  N13: NANO.D3, IC.DATA_IN
  N14: NANO.D4, IC.VDR
  N15: NANO.D5, IC.CLK
  N16: NANO.D6, 6_8kΩ.Pin_1
  N17: NANO.D7, 330Ω.Pin_1
  N18: NANO.A5, J6.pin2
  N19: NANO.A4, J6.pin1
  N20: NANO.A0, PHOTO.pin_0, 100kΩ.Pin_0
  N21: IC.Out_10, JP2.6
  N22: IC.Out_11, JP2.5
  N23: IC.Out_12, JP2.4
  N24: IC.Out_13, JP2.3
  N25: IC.Out_14, JP2.2
  N26: IC.CO, 6_8kΩ.Pin_0
  N27: U1.input_voltage, J2.pin1
  N28: Q1.B, 47kΩ.Pin_1
  N29: Q1.C, 10kΩ.Pin_0
  N30: J1.pin2, 47kΩ.Pin_0
  N31: J7.pin2, 330Ω.Pin_0

notes:
  WILKINSON ENGINEERING
  V1.2

custom parts:
  UAA2022: Motorolla 16 bit seriel LED driver. Can drive up to 16 segments without the need for extrernal current limiting resistors. LED brightness controlled via input voltage in CO pin. Non-multiplexed, therefore no RFI. Cascadable. Datasheet: https://datasheetspdf.com/pdf-file/613601/Motorola/UAA2022/1
